// Logisim project cpu.circ as structural Verilog: 1 circuit, main circuit cpu
module cpu (
  input  clk,
  input  [31:0] Instruction,
  input  [31:0] MemReadData,
  output [31:0] MemAddress,
  output [31:0] ProgramCounter,
  output [31:0] ra,
  output [31:0] sp,
  output [31:0] t0,
  output [31:0] t1,
  output [31:0] t2,
  output [31:0] s0,
  output [31:0] s1,
  output [31:0] a0,
  output [3:0] MemWriteMask,
  output [31:0] MemWriteData
);

  wire Bsel, RegWEn;
  wire [3:0] ALUSel;
  wire [31:0] adder_1_out, ALUresult, imm_data, multiplexer_1_out, r1, r2;

  Register #(.width(32)) PC (.D(adder_1_out), .clk(clk), .Q(ProgramCounter));  // open: en, clr
  Adder #(.width(32)) adder_1 (.a(ProgramCounter), .b(32'h4), .out(adder_1_out));  // open: cin, cout
  control_logic control_logic_1 (
    .Instruction(Instruction), .RegWEn(RegWEn), .BSel(Bsel), .ALUSel(ALUSel));  // open: BrEq, BrLt, PCSel, ImmSel, BrUn, ASel, MemWEn, WBSel
  regfile regfile_1 (
    .ReadIndex1(Instruction[19:15]), .WriteIndex(Instruction[11:7]), .WriteData(ALUresult), .RegWEn(RegWEn),
    .clk(clk), .ra(ra), .sp(sp), .t0(t0), .t1(t1), .t2(t2), .s0(s0), .s1(s1), .a0(a0), .ReadData1(r1),
    .ReadData2(r2));  // open: ReadIndex2
  imm_gen imm_gen_1 (.Instruction(Instruction), .ImmSel(3'b000), .Immediate(imm_data));
  Multiplexer #(.width(32)) multiplexer_1 (.in0(r2), .in1(imm_data), .out(multiplexer_1_out), .sel(Bsel));
  alu alu_1 (.A(r1), .B(multiplexer_1_out), .ALUSel(ALUSel), .ALUResult(ALUresult));
  // branch_comp branch_comp_1: pin names not known
  // partial_store partial_store_1: pin names not known
  // partial_load partial_load_1: pin names not known

  // Notes on the sheet:
  //   To IMEM
  //   IMEM (do **NOT** move this)
  //   From IMEM
  //   Inputs/Outputs for testing. Do **NOT** move these.
  //   It is OK to move the PC, RegFile, ALU, MEM, Branch Comp, Imm Gen, Partial Load, Partial Store and Control Logic to wherever is most convenient for you when constructing your CPU, and to delete this text
  //   To DMEM
  //   DMEM (do **NOT** move this)
  //   From DMEM
endmodule
